// Logisim project processador.circ as structural Verilog: 4 circuits, main circuit main
module main (
  input  in_1,
  output [7:0] out_2,
  output [7:0] out_3,
  output [7:0] out_4
);

  wire Beq, Bge, Branch, clock_1_out, Jump, ula_1_igual, ula_1_maior, unidadecontrole_1_store,
       unidadecontrole_1_writeornotreg, unidadecontrole_1_writereg;
  wire [2:0] unidadecontrole_1_soma0;
  wire [7:0] adder_1_out, bit_extender_1_out, bit_extender_2_out, bit_extender_3_out, multiplexer_1_out,
       multiplexer_2_out, multiplexer_3_out, multiplexer_4_out, multiplexer_5_out, PC_q, ram_1_data, ula_1_r;
  wire [15:0] rom_1_data;

  Register PC (.D(multiplexer_1_out), .Q(PC_q), .clk(clock_1_out), .clr(in_1));  // open: en
  Adder adder_1 (.a(8'h1), .b(PC_q), .out(adder_1_out));  // open: cin, cout
  ROM #(.dataWidth(16)) rom_1 (.addr(PC_q), .data(rom_1_data));  // open: sel
  Clock clock_1 (.out(clock_1_out));
  Multiplexer #(.width(8), .enable("false")) multiplexer_1 (
    .in0(multiplexer_5_out), .in1(bit_extender_1_out), .out(multiplexer_1_out), .sel(Bge));
  registradores Registradores (
    .Read_reg_1(rom_1_data[7:4]), .Read_reg_2(rom_1_data[3:0]), .Write_data(multiplexer_3_out),
    .Write_reg(rom_1_data[11:8]), .RegWrite(unidadecontrole_1_writeornotreg), .CLOCK(clock_1_out),
    .CLEAR(1'b0), .Read_data_1(out_2), .Read_data_2(out_4));
  UnidadeControle unidadecontrole_1 (
    .a(rom_1_data[15]), .b(rom_1_data[14]), .c(rom_1_data[13]), .d(rom_1_data[12]),
    .Store(unidadecontrole_1_store), .WriteorNotReg(unidadecontrole_1_writeornotreg),
    .soma0(unidadecontrole_1_soma0[0]), .soma1(unidadecontrole_1_soma0[1]),
    .soma2(unidadecontrole_1_soma0[2]), .Writereg(unidadecontrole_1_writereg), .Beq(Beq), .Bge(Bge),
    .J(Jump), .Branch(Branch));
  assign bit_extender_1_out = {{4{1'b0}}, rom_1_data[3:0]};  // Bit_Extender bit_extender_1
  Multiplexer #(.width(8), .enable("false")) multiplexer_2 (
    .in0(bit_extender_1_out), .in1(out_4), .out(multiplexer_2_out), .sel(Bge));
  ULA ula_1 (
    .A(out_2), .B(multiplexer_2_out), .\Função (unidadecontrole_1_soma0), .R(ula_1_r), .Maior(ula_1_maior),
    .Igual(ula_1_igual));  // open: Shamt
  RAM #(.bus("separate")) ram_1 (
    .addr(out_4), .din(out_2), .data(ram_1_data), .str(unidadecontrole_1_store), .sel(1'b1),
    .clk(clock_1_out), .ld(1'b1));  // open: clr
  assign bit_extender_2_out = {{7{1'b0}}, ula_1_maior};  // Bit_Extender bit_extender_2
  assign bit_extender_3_out = {{7{1'b0}}, ula_1_igual};  // Bit_Extender bit_extender_3
  Multiplexer #(.width(8), .enable("false")) multiplexer_3 (
    .in0(ram_1_data), .in1(ula_1_r), .out(multiplexer_3_out), .sel(unidadecontrole_1_writereg));
  Multiplexer #(.width(8), .enable("false")) multiplexer_4 (
    .in0(bit_extender_2_out), .in1(bit_extender_3_out), .out(multiplexer_4_out), .sel(Branch));
  Multiplexer #(.width(8), .enable("false")) multiplexer_5 (
    .in0(adder_1_out), .in1(multiplexer_4_out), .out(multiplexer_5_out), .sel(Jump));

  // Notes on the sheet:
  //   contents of rom_1 (hex, n*v repeats v):
  //   3010 2510 215 8 1239 4239
endmodule

module registradores (
  input  [3:0] Read_reg_1,
  input  [3:0] Read_reg_2,
  input  [7:0] Write_data,
  input  [3:0] Write_reg,
  input  RegWrite,
  input  CLOCK,
  input  CLEAR,
  output [7:0] Read_data_1,
  output [7:0] Read_data_2
);

  wire WE0, WE1, WE2, WE3, WE4, WE5, WE6, WE7;
  wire [7:0] demultiplexer_2_out0, demultiplexer_2_out1, demultiplexer_2_out2, demultiplexer_2_out3,
       demultiplexer_2_out4, demultiplexer_2_out5, demultiplexer_2_out6, demultiplexer_2_out7, Reg0, Reg1,
       Reg2, Reg3, Reg4, Reg5, Reg6, Reg7;

  Demultiplexer #(.select(4), .enable("false")) demultiplexer_1 (
    .out0(WE0), .out1(WE1), .out2(WE2), .out3(WE3), .out4(WE4), .out5(WE5), .out6(WE6), .out7(WE7),
    .in(RegWrite), .sel(Write_reg));  // open: out8, out9, out10, out11, out12, out13, out14, out15
  Demultiplexer #(.select(4), .width(8), .enable("false")) demultiplexer_2 (
    .out0(demultiplexer_2_out0), .out1(demultiplexer_2_out1), .out2(demultiplexer_2_out2),
    .out3(demultiplexer_2_out3), .out4(demultiplexer_2_out4), .out5(demultiplexer_2_out5),
    .out6(demultiplexer_2_out6), .out7(demultiplexer_2_out7), .in(Write_data), .sel(Write_reg));  // open: out8, out9, out10, out11, out12, out13, out14, out15
  Register Reg_0 (.D(demultiplexer_2_out0), .en(WE0), .Q(Reg0), .clk(CLOCK), .clr(CLEAR));
  Register Reg_1 (.D(demultiplexer_2_out1), .en(WE1), .Q(Reg1), .clk(CLOCK), .clr(CLEAR));
  Register Reg_2 (.D(demultiplexer_2_out2), .en(WE2), .Q(Reg2), .clk(CLOCK), .clr(CLEAR));
  Register Reg_3 (.D(demultiplexer_2_out3), .en(WE3), .Q(Reg3), .clk(CLOCK), .clr(CLEAR));
  Register Reg_4 (.D(demultiplexer_2_out4), .en(WE4), .Q(Reg4), .clk(CLOCK), .clr(CLEAR));
  Register Reg_5 (.D(demultiplexer_2_out5), .en(WE5), .Q(Reg5), .clk(CLOCK), .clr(CLEAR));
  Register Reg_6 (.D(demultiplexer_2_out6), .en(WE6), .Q(Reg6), .clk(CLOCK), .clr(CLEAR));
  Register Reg_7 (.D(demultiplexer_2_out7), .en(WE7), .Q(Reg7), .clk(CLOCK), .clr(CLEAR));
  Multiplexer #(.select(4), .width(8), .enable("false")) multiplexer_1 (
    .in0(Reg0), .in1(Reg1), .in2(Reg2), .in3(Reg3), .in4(Reg4), .in5(Reg5), .in6(Reg6), .in7(Reg7),
    .out(Read_data_1), .sel(Read_reg_1));  // open: in8, in9, in10, in11, in12, in13, in14, in15
  Multiplexer #(.select(4), .width(8), .enable("false")) multiplexer_2 (
    .in0(Reg0), .in1(Reg1), .in2(Reg2), .in3(Reg3), .in4(Reg4), .in5(Reg5), .in6(Reg6), .in7(Reg7),
    .out(Read_data_2), .sel(Read_reg_2));  // open: in8, in9, in10, in11, in12, in13, in14, in15

  // Other names for the same wires on the sheet: Read1[3:0] = Read_reg_1; Read2[3:0] = Read_reg_2
endmodule

module ULA (
  input  [7:0] A,
  input  [7:0] B,
  input  [2:0] \Função ,
  input  [2:0] Shamt,
  output [7:0] R,
  output Maior,
  output Igual
);

  wire [7:0] AComp, adder_1_out, ADiv, AMult, ANeg, AShiftDir, AShiftEsq, ASoma, ASub, BComp, BDiv,
       bit_extender_1_out, BMult, BSoma, BSub, divider_1_out, multiplier_1_out, negator_1_out, shifter_1_out,
       shifter_2_out, subtractor_1_out;

  Demultiplexer #(.select(3), .width(8), .enable("false")) demultiplexer_1 (
    .out0(ASoma), .out1(ASub), .out2(AMult), .out3(ADiv), .out4(ANeg), .out5(AComp), .out6(AShiftEsq),
    .out7(AShiftDir), .in(A), .sel(\Função ));
  Demultiplexer #(.select(3), .width(8), .enable("false")) demultiplexer_2 (
    .out0(BSoma), .out1(BSub), .out2(BMult), .out3(BDiv), .out5(BComp), .in(B), .sel(\Função ));  // open: out4, out6, out7
  Adder adder_1 (.a(ASoma), .b(BSoma), .out(adder_1_out));  // open: cin, cout
  Subtractor subtractor_1 (.a(ASub), .b(BSub), .out(subtractor_1_out));  // open: bin, bout
  Multiplier multiplier_1 (.a(AMult), .b(BMult), .out(multiplier_1_out));  // open: cin, cout
  Divider divider_1 (.a(ADiv), .b(BDiv), .out(divider_1_out));  // open: upper, rem
  Negator negator_1 (.in(ANeg), .out(negator_1_out));
  Comparator comparator_1 (.a(AComp), .b(BComp), .gt(Maior), .eq(Igual));  // open: lt
  Shifter shifter_1 (.in(AShiftEsq), .\dist (Shamt), .out(shifter_1_out));
  Shifter #(.shift("lr")) shifter_2 (.in(AShiftDir), .\dist (Shamt), .out(shifter_2_out));
  assign bit_extender_1_out = {{7{1'b0}}, Igual};  // Bit_Extender bit_extender_1
  Multiplexer #(.select(3), .width(8), .enable("false")) multiplexer_1 (
    .in0(adder_1_out), .in1(subtractor_1_out), .in2(multiplier_1_out), .in3(divider_1_out),
    .in4(negator_1_out), .in5(bit_extender_1_out), .in6(shifter_1_out), .in7(shifter_2_out), .out(R),
    .sel(\Função ));
endmodule

module UnidadeControle (
  input  a,
  input  b,
  input  c,
  input  d,
  output Store,
  output WriteorNotReg,
  output soma0,
  output soma1,
  output soma2,
  output Writereg,
  output Beq,
  output Bge,
  output J,
  output Branch
);

  wire not_1_out, not_2_out, not_3_out, not_5_out, not_6_out, not_7_out, not_8_out, not_9_out, not_10_out,
       not_11_out;

  not not_1 (not_1_out, a);
  and and_1 (WriteorNotReg, not_1_out, not_2_out, not_3_out);
  not not_2 (not_2_out, b);
  not not_3 (not_3_out, d);
  not not_4 (Writereg, c);
  not not_5 (not_5_out, a);
  not not_6 (not_6_out, b);
  not not_7 (not_7_out, a);
  not not_8 (not_8_out, c);
  not not_9 (not_9_out, d);
  not not_10 (not_10_out, a);
  not not_11 (not_11_out, d);
  not not_12 (Branch, b);
  and and_2 (Beq, not_5_out, not_6_out, c, d);
  and and_3 (Bge, not_7_out, b, not_8_out, not_9_out);
  and and_4 (J, not_10_out, b, c, not_11_out);

  assign soma0 = 1'b0;
  assign soma1 = 1'b0;
  assign soma2 = 1'b0;
  assign Store = d;
endmodule
