// Logisim project processador.circ as structural Verilog: 5 circuits, main circuit main
module main (
  input  in_1,
  output [15:0] out_2,
  output [15:0] out_3
);

  wire and_1_out, Branch, clock_1_out, Jump, li, MemRead, not_1_out, or_1_out, or_2_out, RegWrit,
       ula_1_igual, ula_1_maior, unidadecontrole_1_store, unidadecontrole_1_writereg;
  wire [2:0] functCtrl;
  wire [3:0] Opcode, R0, R1, R2;
  wire [15:0] adder_1_out, bit_extender_1_out, multiplexer_2_out, PC_q, ram_1_data,
       Registradores_read_data_1, Registradores_read_data_2, ula_1_r, WriteData;

  Register #(.width(16)) PC (.D(multiplexer_2_out), .Q(PC_q), .clk(clock_1_out), .clr(in_1));  // open: en
  Adder #(.width(16)) adder_1 (.a(16'h1), .b(PC_q), .out(adder_1_out));  // open: cin, cout
  ROM #(.addrWidth(16), .dataWidth(16)) rom_1 (.addr(PC_q), .data({Opcode, R0, R1, R2}));  // open: sel
  Register register_1 ();  // open: D, en, Q, clk, clr
  Clock clock_1 (.out(clock_1_out));
  UnidadeControle unidadecontrole_1 (
    .a(Opcode[3]), .b(Opcode[2]), .c(Opcode[1]), .d(Opcode[0]), .Store(unidadecontrole_1_store),
    .WriteonRegorNot(RegWrit), .Writereg(unidadecontrole_1_writereg), .J(Jump), .Branch(Branch),
    .functCtrl1(functCtrl[0]), .functCtrl2(functCtrl[1]), .functCtrl3(functCtrl[2]), .Li(li),
    .MemRead(MemRead));  // open: Beq, Bge
  registradores Registradores (
    .Read_reg_1(R2), .Read_reg_2(R1), .Write_data(WriteData), .Write_reg(R0), .RegWrite(RegWrit),
    .CLOCK(clock_1_out), .CLEAR(1'b0), .Read_data_1(Registradores_read_data_1),
    .Read_data_2(Registradores_read_data_2));
  assign bit_extender_1_out = {{12{1'b0}}, R2};  // Bit_Extender bit_extender_1
  not not_1 (not_1_out, clock_1_out);
  ULA ula_1 (
    .A(bit_extender_1_out), .B(Registradores_read_data_2), .\Função (functCtrl), .R(ula_1_r),
    .maior(ula_1_maior), .Igual(ula_1_igual));  // open: Soma, Comp
  RAM #(.addrWidth(16), .dataWidth(16), .bus("separate")) ram_1 (
    .addr(Registradores_read_data_2), .din(Registradores_read_data_1), .data(ram_1_data),
    .str(unidadecontrole_1_store), .clk(not_1_out), .ld(MemRead));  // open: sel, clr
  or or_1 (or_1_out, ula_1_maior, ula_1_igual);
  Multiplexer #(.width(16), .enable("false")) multiplexer_1 (
    .in0(ram_1_data), .in1(ula_1_r), .out(WriteData), .sel(unidadecontrole_1_writereg));
  or or_2 (or_2_out, Jump, and_1_out);
  and and_1 (and_1_out, or_1_out, Branch);
  Multiplexer #(.width(16), .enable("false")) multiplexer_2 (
    .in0(adder_1_out), .in1(bit_extender_1_out), .out(multiplexer_2_out), .sel(or_2_out));

  // Notes on the sheet:
  //   contents of rom_1 (hex, n*v repeats v):
  //   7700 2070 109 774 110c 2270 4029 5020 11f 774 6500
endmodule

module registradores (
  input  [3:0] Read_reg_1,
  input  [3:0] Read_reg_2,
  input  [15:0] Write_data,
  input  [3:0] Write_reg,
  input  RegWrite,
  input  CLOCK,
  input  CLEAR,
  output [15:0] Read_data_1,
  output [15:0] Read_data_2
);

  wire WE0, WE1, WE2, WE3, WE4, WE5, WE6, WE7;
  wire [15:0] demultiplexer_2_out0, demultiplexer_2_out1, demultiplexer_2_out2, demultiplexer_2_out3,
       demultiplexer_2_out4, demultiplexer_2_out5, demultiplexer_2_out6, demultiplexer_2_out7, Reg0, Reg1,
       Reg2, Reg3, Reg4, Reg5, Reg6, Reg7;

  Demultiplexer #(.select(4), .enable("false")) demultiplexer_1 (
    .out0(WE0), .out1(WE1), .out2(WE2), .out3(WE3), .out4(WE4), .out5(WE5), .out6(WE6), .out7(WE7),
    .in(RegWrite), .sel(Write_reg));  // open: out8, out9, out10, out11, out12, out13, out14, out15
  Demultiplexer #(.select(4), .width(16), .enable("false")) demultiplexer_2 (
    .out0(demultiplexer_2_out0), .out1(demultiplexer_2_out1), .out2(demultiplexer_2_out2),
    .out3(demultiplexer_2_out3), .out4(demultiplexer_2_out4), .out5(demultiplexer_2_out5),
    .out6(demultiplexer_2_out6), .out7(demultiplexer_2_out7), .in(Write_data), .sel(Write_reg));  // open: out8, out9, out10, out11, out12, out13, out14, out15
  Register #(.width(16)) Reg_0 (.D(demultiplexer_2_out0), .en(WE0), .Q(Reg0), .clk(CLOCK), .clr(CLEAR));
  Register #(.width(16)) Reg_1 (.D(demultiplexer_2_out1), .en(WE1), .Q(Reg1), .clk(CLOCK), .clr(CLEAR));
  Register #(.width(16)) Reg_2 (.D(demultiplexer_2_out2), .en(WE2), .Q(Reg2), .clk(CLOCK), .clr(CLEAR));
  Register #(.width(16)) Reg_3 (.D(demultiplexer_2_out3), .en(WE3), .Q(Reg3), .clk(CLOCK), .clr(CLEAR));
  Register #(.width(16)) Reg_4 (.D(demultiplexer_2_out4), .en(WE4), .Q(Reg4), .clk(CLOCK), .clr(CLEAR));
  Register #(.width(16)) Reg_5 (.D(demultiplexer_2_out5), .en(WE5), .Q(Reg5), .clk(CLOCK), .clr(CLEAR));
  Register #(.width(16)) Reg_6 (.D(demultiplexer_2_out6), .en(WE6), .Q(Reg6), .clk(CLOCK), .clr(CLEAR));
  Register #(.width(16)) Reg_7 (.D(demultiplexer_2_out7), .en(WE7), .Q(Reg7), .clk(CLOCK), .clr(CLEAR));
  Multiplexer #(.select(4), .width(16), .enable("false")) multiplexer_1 (
    .in0(Reg0), .in1(Reg1), .in2(Reg2), .in3(Reg3), .in4(Reg4), .in5(Reg5), .in6(Reg6), .in7(Reg7),
    .out(Read_data_1), .sel(Read_reg_1));  // open: in8, in9, in10, in11, in12, in13, in14, in15
  Multiplexer #(.select(4), .width(16), .enable("false")) multiplexer_2 (
    .in0(Reg0), .in1(Reg1), .in2(Reg2), .in3(Reg3), .in4(Reg4), .in5(Reg5), .in6(Reg6), .in7(Reg7),
    .out(Read_data_2), .sel(Read_reg_2));  // open: in8, in9, in10, in11, in12, in13, in14, in15

  // Other names for the same wires on the sheet: Read1[3:0] = Read_reg_1; Read2[3:0] = Read_reg_2
endmodule

module ULA (
  input  [15:0] A,
  input  [15:0] B,
  input  [2:0] \Função ,
  input  Soma,
  input  Comp,
  output [15:0] R,
  output maior,
  output Igual
);

  wire [3:0] undriven;
  wire [7:0] bit_extender_1_out;
  wire [15:0] AComp, adder_1_out, ADiv, AMult, ANeg, AShiftDir, AShiftEsq, ASoma, ASub, BComp, BDiv, BMult,
       BSoma, BSub, divider_1_out, multiplier_1_out, negator_1_out, subtractor_1_out, undriven_2, undriven_3;

  Demultiplexer #(.select(3), .width(16), .enable("false")) demultiplexer_1 (
    .out0(ASoma), .out1(ASub), .out2(AMult), .out3(ADiv), .out4(ANeg), .out5(AComp), .out6(AShiftEsq),
    .out7(AShiftDir), .in(A), .sel(\Função ));
  Demultiplexer #(.select(3), .width(16), .enable("false")) demultiplexer_2 (
    .out0(BSoma), .out1(BSub), .out2(BMult), .out3(BDiv), .out5(BComp), .in(B), .sel(\Função ));  // open: out4, out6, out7
  assign bit_extender_1_out = {{7{1'b0}}, Comp};  // Bit_Extender bit_extender_1
  Adder #(.width(16)) adder_1 (.a(ASoma), .b(BSoma), .out(adder_1_out));  // open: cin, cout
  Subtractor #(.width(16)) subtractor_1 (.a(ASub), .b(BSub), .out(subtractor_1_out));  // open: bin, bout
  Multiplier #(.width(16)) multiplier_1 (.a(AMult), .b(BMult), .out(multiplier_1_out));  // open: cin, cout
  Divider #(.width(16)) divider_1 (.a(ADiv), .b(BDiv), .out(divider_1_out));  // open: upper, rem
  Negator #(.width(16)) negator_1 (.in(ANeg), .out(negator_1_out));
  Comparator #(.width(16)) comparator_1 (.a(AComp), .b(BComp), .gt(maior), .eq(Igual));  // open: lt
  Shifter #(.width(16)) shifter_1 (.in(AShiftEsq), .\dist (undriven));  // open: out
  Shifter #(.width(16), .shift("lr")) shifter_2 (.in(AShiftDir), .\dist (undriven));  // open: out
  Bit_Extender #(.in_width(1), .out_width(8)) bit_extender_2 (.in(maior));  // open: out
  Multiplexer #(.select(3), .width(16), .enable("false")) multiplexer_1 (
    .in0(adder_1_out), .in1(subtractor_1_out), .in2(multiplier_1_out), .in3(divider_1_out),
    .in4(negator_1_out), .in5(undriven_2), .in7(undriven_3), .out(R), .sel(\Função ));  // open: in6
endmodule

module UnidadeControle (
  input  a,
  input  b,
  input  c,
  input  d,
  output Store,
  output WriteonRegorNot,
  output Writereg,
  output Beq,
  output Bge,
  output J,
  output Branch,
  output functCtrl1,
  output functCtrl2,
  output functCtrl3,
  output Li,
  output MemRead
);

  wire and_1_out, and_2_out, and_3_out, and_4_out, and_5_out, and_6_out, and_7_out, and_8_out, and_9_out,
       and_10_out, and_14_out, and_15_out, not_1_out, not_2_out, not_3_out, not_4_out, not_5_out, not_6_out,
       not_7_out, not_9_out, not_10_out, not_11_out, not_12_out, not_13_out, not_14_out, not_15_out,
       not_16_out, not_17_out, not_18_out, not_19_out, not_20_out, not_21_out, not_22_out, not_23_out,
       not_24_out, not_25_out, not_26_out, not_27_out, not_28_out, not_29_out, not_30_out;

  not not_1 (not_1_out, b);
  and and_1 (and_1_out, not_1_out, c, d);
  and and_2 (and_2_out, b, not_2_out, d);
  not not_2 (not_2_out, c);
  and and_3 (and_3_out, a, d);
  not not_3 (not_3_out, a);
  not not_4 (not_4_out, b);
  and and_4 (and_4_out, not_3_out, not_4_out, not_5_out);
  not not_5 (not_5_out, d);
  not not_6 (not_6_out, a);
  and and_5 (and_5_out, not_6_out, c, not_7_out);
  not not_7 (not_7_out, d);
  not not_8 (Writereg, c);
  not not_9 (not_9_out, a);
  not not_10 (not_10_out, b);
  not not_11 (not_11_out, c);
  not not_12 (not_12_out, a);
  not not_13 (not_13_out, c);
  not not_14 (not_14_out, d);
  not not_15 (not_15_out, a);
  not not_16 (not_16_out, d);
  not not_17 (not_17_out, a);
  not not_18 (not_18_out, b);
  not not_19 (not_19_out, c);
  not not_20 (not_20_out, a);
  not not_21 (not_21_out, c);
  not not_22 (not_22_out, d);
  and and_6 (and_6_out, b, not_23_out);
  not not_23 (not_23_out, c);
  and and_7 (and_7_out, a, not_24_out);
  not not_24 (not_24_out, c);
  and and_8 (and_8_out, a, b);
  and and_9 (and_9_out, b, not_25_out);
  not not_25 (not_25_out, c);
  and and_10 (and_10_out, a, b);
  not not_26 (not_26_out, a);
  not not_27 (not_27_out, d);
  not not_28 (not_28_out, a);
  not not_29 (not_29_out, b);
  not not_30 (not_30_out, d);
  or or_1 (Store, and_1_out, and_2_out, and_3_out);
  or or_2 (WriteonRegorNot, and_4_out, and_5_out);
  and and_11 (Beq, not_9_out, not_10_out, not_11_out, d);
  and and_12 (Bge, not_12_out, b, not_13_out, not_14_out);
  and and_13 (J, not_15_out, b, c, not_16_out);
  and and_14 (and_14_out, not_17_out, not_18_out, not_19_out, d);
  or or_3 (Branch, and_14_out, and_15_out);
  and and_15 (and_15_out, not_20_out, b, not_21_out, not_22_out);
  or or_4 (functCtrl1, d, and_6_out, and_7_out, and_8_out);
  or or_5 (functCtrl3, d, and_9_out, and_10_out);
  and and_16 (Li, not_26_out, b, c, not_27_out);
  and and_17 (MemRead, not_28_out, not_29_out, c, not_30_out);

  assign functCtrl2 = 1'b0;
endmodule

module Controle_ULA (
  input  [2:0] funct,
  input  [1:0] ALUOp,
  output [2:0] ULACtrl
);

  Multiplexer #(.select(2), .width(3), .enable("false")) multiplexer_1 (
    .in0(3'b000), .in1(3'b101), .in2(funct), .in3(3'b000), .out(ULACtrl), .sel(ALUOp));
endmodule
